// Logisim project SAP_1_automatic_20.circ as structural Verilog: 13 circuits, main circuit main
module main (
  input  in_1,
  input  in_2,
  input  in_3,
  output [3:0] out_4,
  output [7:0] out_5,
  output [7:0] out_6,
  output [7:0] out_7,
  output [7:0] out_8,
  output [7:0] out_9,
  output [7:0] out_10,
  output [7:0] out_11,
  output [7:0] out_12,
  output [7:0] out_13,
  output [7:0] out_14,
  output [7:0] out_15,
  output [7:0] out_16,
  output [7:0] out_17,
  output [7:0] out_18,
  output [7:0] out_19,
  output [7:0] out_20,
  output [7:0] out_21,
  output [7:0] out_22,
  output [7:0] out_23,
  output [7:0] out_24,
  output [3:0] out_25,
  output [3:0] out_26,
  output [7:0] out_27,
  output [3:0] out_28
);

  wire a_in, a_out, alu_out, alu_sub, b_in, b_out, hlt, ins_reg_in_en, ins_reg_out_en, jmp_en, L1, L2,
       mar_in_en, pc_en, pc_out, sram_rd, sram_wr;
  wire [7:0] debug_data, multiplexer_1_out;
  wire [7:4] undriven;

  Hex_Digit_Display hex_digit_display_1 (.value(multiplexer_1_out[7:4]));  // open: dp
  Hex_Digit_Display hex_digit_display_2 (.value(multiplexer_1_out[3:0]));  // open: dp
  Multiplexer #(.width(8)) multiplexer_1 (.in0(out_5), .in1({undriven, out_28}), .out(multiplexer_1_out), .sel(in_1));
  Hex_Digit_Display hex_digit_display_3 (.value(out_28));  // open: dp
  ins_loader ins_loader_1 (
    .bc_reset(in_2), .bc_enable(L2), .clk(in_3), .debug(in_1), .bc_address(out_28), .L1(L1), .L2(L2));
  Hex_Digit_Display hex_digit_display_4 (.value(out_4));  // open: dp
  pc_with_loader pc_with_loader_1 (
    .pc_reset(in_2), .load_or_count(jmp_en), .pc_en(pc_en), .clk(in_3), .data_load(out_5[3:0]),
    .pc_out_en(pc_out), .pc_value(out_4), .pc_out(out_5[3:0]));
  sram sram_1 (
    .sram_rd(sram_rd), .sram_wr(sram_wr), .sram_d_in(out_5), .mar_d_in(multiplexer_1_out),
    .mar_in_en(mar_in_en), .sram_clk(in_3), .sram_d_out(out_5), .out_8(out_8), .out_9(out_9),
    .out_10(out_10), .out_11(out_11), .out_12(out_12), .out_13(out_14), .out_14(out_15), .out_15(out_16),
    .out_16(out_17), .out_17(out_18), .out_18(out_19), .out_19(out_20), .out_20(out_21), .out_21(out_22),
    .out_22(out_23), .out_23(out_24));
  ROM #(.addrWidth(4)) rom_1 (.addr(out_28), .data(debug_data));
  Hex_Digit_Display hex_digit_display_5 (.value(out_5[7:4]));  // open: dp
  Hex_Digit_Display hex_digit_display_6 (.value(out_5[3:0]));  // open: dp
  assign out_5 = in_1 ? debug_data : 8'bz;  // Controlled_Buffer controlled_buffer_1
  Hex_Digit_Display hex_digit_display_7 (.value(out_5[3:0]));  // open: dp
  reg_gp reg_gp_1 (
    .reg_in(out_5), .reg_in_en(a_in), .reg_clk(in_3), .reg_out_en(a_out), .reg_int_out(out_6), .reg_out(out_5));
  reg_gp reg_gp_2 (
    .reg_in(out_5), .reg_in_en(b_in), .reg_clk(in_3), .reg_out_en(b_out), .reg_int_out(out_13),
    .reg_out(out_5));
  Ins_reg ins_reg_1 (
    .ins_reg_in(out_5), .ins_reg_in_en(ins_reg_in_en), .clk(in_3), .ins_reg_out_en(ins_reg_out_en),
    .add_outs(out_5[3:0]), .ins_out(out_26));
  Hex_Digit_Display hex_digit_display_8 (.value(out_26));  // open: dp
  Hex_Digit_Display hex_digit_display_9 (.value(out_13[7:4]));  // open: dp
  Hex_Digit_Display hex_digit_display_10 (.value(out_6[7:4]));  // open: dp
  Hex_Digit_Display hex_digit_display_11 (.value(out_13[3:0]));  // open: dp
  Hex_Digit_Display hex_digit_display_12 (.value(out_6[3:0]));  // open: dp
  alu alu_1 (
    .alu_in_1(out_6), .alu_out_en(alu_out), .alu_sub(alu_sub), .alu_in_2(out_13), .alu_out(out_5));  // open: alu_carry_out
  control_sequence control_sequence_1 (
    .clk(in_3), .clk_reset(in_2), .ins_msb(out_26), .L1(L1), .debug(in_1), .l2(L2),
    .mar_in_en_final(mar_in_en), .pc_en(pc_en), .pc_out_final(pc_out), .sram_rd_final(sram_rd),
    .jmp_en(jmp_en), .ins_reg_in_en(ins_reg_in_en), .hlt(hlt), .a_in(a_in), .a_out_final(a_out), .b_in(b_in),
    .sub_out(alu_sub), .ins_reg_out_en(ins_reg_out_en), .sram_wr_final(sram_wr), .alu_out(alu_out));
  LED led_1 (.in(in_1));

  assign out_7 = out_5;
  assign out_25 = out_5[3:0];
  assign out_27 = out_5;

  // Other names for the same wires on the sheet: bc_address[3:0] = out_28; clk = in_3; debug = in_1;
  //   ir_operand[3:0] = out_5[3:0]; pc_reset = in_2

  // Notes on the sheet:
  //   MAR value
  //   counter value
  //   contents of rom_1 (hex, n*v repeats v):
  //   1d 2e 65 0 0 30 5f f0 5*0 14 19
  //   Data bus
  //   loader counter value
  //   linstruction operand
  //   linstruction opcoder
  //   REG A
  //   REG B
  //   Code loading mode LED
  //   Code loading pin
  //   Clock and Rest
endmodule

module dec_4x16 (
  input  [3:0] dec_sel,
  output [15:0] dec_out
);

  wire not_1_out, not_2_out, not_3_out, not_4_out;

  not not_1 (not_1_out, dec_sel[3]);
  not not_2 (not_2_out, dec_sel[2]);
  not not_3 (not_3_out, dec_sel[1]);
  not not_4 (not_4_out, dec_sel[0]);
  and and_1 (dec_out[0], not_4_out, not_3_out, not_2_out, not_1_out);
  and and_2 (dec_out[1], dec_sel[0], not_3_out, not_2_out, not_1_out);
  and and_3 (dec_out[2], not_4_out, dec_sel[1], not_2_out, not_1_out);
  and and_4 (dec_out[3], dec_sel[0], dec_sel[1], not_2_out, not_1_out);
  and and_5 (dec_out[4], not_4_out, not_3_out, dec_sel[2], not_1_out);
  and and_6 (dec_out[5], dec_sel[0], not_3_out, dec_sel[2], not_1_out);
  and and_7 (dec_out[6], not_4_out, dec_sel[1], dec_sel[2], not_1_out);
  and and_8 (dec_out[7], dec_sel[0], dec_sel[1], dec_sel[2], not_1_out);
  and and_9 (dec_out[8], not_4_out, not_3_out, not_2_out, dec_sel[3]);
  and and_10 (dec_out[9], dec_sel[0], not_3_out, not_2_out, dec_sel[3]);
  and and_11 (dec_out[10], not_4_out, dec_sel[1], not_2_out, dec_sel[3]);
  and and_12 (dec_out[11], dec_sel[0], dec_sel[1], not_2_out, dec_sel[3]);
  and and_13 (dec_out[12], not_4_out, not_3_out, dec_sel[2], dec_sel[3]);
  and and_14 (dec_out[13], dec_sel[0], not_3_out, dec_sel[2], dec_sel[3]);
  and and_15 (dec_out[14], not_4_out, dec_sel[1], dec_sel[2], dec_sel[3]);
  and and_16 (dec_out[15], dec_sel[0], dec_sel[1], dec_sel[2], dec_sel[3]);
endmodule

module reg_gp (
  input  [7:0] reg_in,
  input  reg_in_en,
  input  reg_clk,
  input  reg_out_en,
  output [7:0] reg_int_out,
  output [7:0] reg_out
);

  wire multiplexer_1_out, multiplexer_2_out, multiplexer_3_out, multiplexer_4_out, multiplexer_5_out,
       multiplexer_6_out, multiplexer_7_out, multiplexer_8_out;

  Multiplexer multiplexer_1 (.in0(reg_int_out[7]), .in1(reg_in[7]), .out(multiplexer_1_out), .sel(reg_in_en));
  D_Flip_Flop d_ff_1 (.D(multiplexer_1_out), .clk(reg_clk), .Q(reg_int_out[7]));  // open: Qn, preset, reset
  Multiplexer multiplexer_2 (.in0(reg_int_out[6]), .in1(reg_in[6]), .out(multiplexer_2_out), .sel(reg_in_en));
  assign reg_out[7] = reg_out_en ? reg_int_out[7] : 1'bz;  // Controlled_Buffer controlled_buffer_1
  D_Flip_Flop d_ff_2 (.D(multiplexer_2_out), .clk(reg_clk), .Q(reg_int_out[6]));  // open: Qn, preset, reset
  assign reg_out[6] = reg_out_en ? reg_int_out[6] : 1'bz;  // Controlled_Buffer controlled_buffer_2
  Multiplexer multiplexer_3 (.in0(reg_int_out[5]), .in1(reg_in[5]), .out(multiplexer_3_out), .sel(reg_in_en));
  D_Flip_Flop d_ff_3 (.D(multiplexer_3_out), .clk(reg_clk), .Q(reg_int_out[5]));  // open: Qn, preset, reset
  assign reg_out[5] = reg_out_en ? reg_int_out[5] : 1'bz;  // Controlled_Buffer controlled_buffer_3
  Multiplexer multiplexer_4 (.in0(reg_int_out[4]), .in1(reg_in[4]), .out(multiplexer_4_out), .sel(reg_in_en));
  D_Flip_Flop d_ff_4 (.D(multiplexer_4_out), .clk(reg_clk), .Q(reg_int_out[4]));  // open: Qn, preset, reset
  assign reg_out[4] = reg_out_en ? reg_int_out[4] : 1'bz;  // Controlled_Buffer controlled_buffer_4
  Multiplexer multiplexer_5 (.in0(reg_int_out[3]), .in1(reg_in[3]), .out(multiplexer_5_out), .sel(reg_in_en));
  D_Flip_Flop d_ff_5 (.D(multiplexer_5_out), .clk(reg_clk), .Q(reg_int_out[3]));  // open: Qn, preset, reset
  assign reg_out[3] = reg_out_en ? reg_int_out[3] : 1'bz;  // Controlled_Buffer controlled_buffer_5
  Multiplexer multiplexer_6 (.in0(reg_int_out[2]), .in1(reg_in[2]), .out(multiplexer_6_out), .sel(reg_in_en));
  D_Flip_Flop d_ff_6 (.D(multiplexer_6_out), .clk(reg_clk), .Q(reg_int_out[2]));  // open: Qn, preset, reset
  assign reg_out[2] = reg_out_en ? reg_int_out[2] : 1'bz;  // Controlled_Buffer controlled_buffer_6
  Multiplexer multiplexer_7 (.in0(reg_int_out[1]), .in1(reg_in[1]), .out(multiplexer_7_out), .sel(reg_in_en));
  D_Flip_Flop d_ff_7 (.D(multiplexer_7_out), .clk(reg_clk), .Q(reg_int_out[1]));  // open: Qn, preset, reset
  Multiplexer multiplexer_8 (.in0(reg_int_out[0]), .in1(reg_in[0]), .out(multiplexer_8_out), .sel(reg_in_en));
  assign reg_out[1] = reg_out_en ? reg_int_out[1] : 1'bz;  // Controlled_Buffer controlled_buffer_7
  D_Flip_Flop d_ff_8 (.D(multiplexer_8_out), .clk(reg_clk), .Q(reg_int_out[0]));  // open: Qn, preset, reset
  assign reg_out[0] = reg_out_en ? reg_int_out[0] : 1'bz;  // Controlled_Buffer controlled_buffer_8

  // Notes on the sheet:
  //                  Input
  //         Input Control 
  //          Clock
  //            Output Control
  //               Memory
  //                      Output
  //                           Internal Output
endmodule

module alu (
  input  [7:0] alu_in_1,
  input  alu_out_en,
  input  alu_sub,
  input  [7:0] alu_in_2,
  output [7:0] alu_out,
  output alu_carry_out
);

  wire adder_2_cout, adder_3_cout, adder_4_cout, adder_5_cout, adder_6_cout, adder_7_cout, adder_8_cout,
       xor_1_out, xor_2_out, xor_3_out, xor_4_out, xor_5_out, xor_6_out, xor_7_out, xor_8_out;
  wire [7:0] adder_8_out;

  xor xor_1 (xor_1_out, alu_in_2[7], alu_sub);
  Adder #(.width(1)) adder_1 (
    .a(alu_in_1[7]), .b(xor_1_out), .out(adder_8_out[7]), .cin(adder_2_cout), .cout(alu_carry_out));
  xor xor_2 (xor_2_out, alu_in_2[6], alu_sub);
  Adder #(.width(1)) adder_2 (
    .a(alu_in_1[6]), .b(xor_2_out), .out(adder_8_out[6]), .cin(adder_3_cout), .cout(adder_2_cout));
  xor xor_3 (xor_3_out, alu_in_2[5], alu_sub);
  Adder #(.width(1)) adder_3 (
    .a(alu_in_1[5]), .b(xor_3_out), .out(adder_8_out[5]), .cin(adder_4_cout), .cout(adder_3_cout));
  xor xor_4 (xor_4_out, alu_in_2[4], alu_sub);
  Adder #(.width(1)) adder_4 (
    .a(alu_in_1[4]), .b(xor_4_out), .out(adder_8_out[4]), .cin(adder_5_cout), .cout(adder_4_cout));
  xor xor_5 (xor_5_out, alu_in_2[3], alu_sub);
  Adder #(.width(1)) adder_5 (
    .a(alu_in_1[3]), .b(xor_5_out), .out(adder_8_out[3]), .cin(adder_6_cout), .cout(adder_5_cout));
  xor xor_6 (xor_6_out, alu_in_2[2], alu_sub);
  Adder #(.width(1)) adder_6 (
    .a(alu_in_1[2]), .b(xor_6_out), .out(adder_8_out[2]), .cin(adder_7_cout), .cout(adder_6_cout));
  xor xor_7 (xor_7_out, alu_in_2[1], alu_sub);
  Adder #(.width(1)) adder_7 (
    .a(alu_in_1[1]), .b(xor_7_out), .out(adder_8_out[1]), .cin(adder_8_cout), .cout(adder_7_cout));
  Adder #(.width(1)) adder_8 (.a(alu_in_1[0]), .b(xor_8_out), .out(adder_8_out[0]), .cin(alu_sub), .cout(adder_8_cout));
  xor xor_8 (xor_8_out, alu_in_2[0], alu_sub);
  assign alu_out = alu_out_en ? adder_8_out : 8'bz;  // Controlled_Buffer controlled_buffer_1

  // Notes on the sheet:
  //              Input 1
  //   Carry Output
  //   Subtract Control
  //                     Full Addres
  //                Output Control
  //                 Alu Output
  //                Input 2
endmodule

module sram_cell (
  input  [7:0] data_in,
  input  wr_en,
  input  clk,
  input  cs,
  input  rd_en,
  output [7:0] memory_content,
  output [7:0] data_out
);

  wire and_1_out, and_2_out;

  and and_1 (and_1_out, wr_en, cs);
  and and_2 (and_2_out, cs, rd_en);
  reg_gp reg_gp_1 (
    .reg_in(data_in), .reg_in_en(and_1_out), .reg_clk(clk), .reg_out_en(and_2_out),
    .reg_int_out(memory_content), .reg_out(data_out));
endmodule

module sram (
  input  sram_rd,
  input  sram_wr,
  input  [7:0] sram_d_in,
  input  [7:0] mar_d_in,
  input  mar_in_en,
  input  sram_clk,
  output [7:0] sram_d_out,
  output [7:0] out_8,
  output [7:0] out_9,
  output [7:0] out_10,
  output [7:0] out_11,
  output [7:0] out_12,
  output [7:0] out_13,
  output [7:0] out_14,
  output [7:0] out_15,
  output [7:0] out_16,
  output [7:0] out_17,
  output [7:0] out_18,
  output [7:0] out_19,
  output [7:0] out_20,
  output [7:0] out_21,
  output [7:0] out_22,
  output [7:0] out_23
);

  wire [7:0] controlled_buffer_1_out, reg_gp_1_reg_int_out;
  wire [15:0] dec_4x16_1_dec_out;

  reg_gp reg_gp_1 (
    .reg_in(mar_d_in), .reg_in_en(mar_in_en), .reg_clk(sram_clk), .reg_int_out(reg_gp_1_reg_int_out));  // open: reg_out_en, reg_out
  dec_4x16 dec_4x16_1 (.dec_sel(reg_gp_1_reg_int_out[3:0]), .dec_out(dec_4x16_1_dec_out));
  assign controlled_buffer_1_out = sram_wr ? sram_d_in : 8'bz;  // Controlled_Buffer controlled_buffer_1
  sram_cell sram_cell_1 (
    .data_in(controlled_buffer_1_out), .wr_en(sram_wr), .clk(sram_clk), .cs(dec_4x16_1_dec_out[0]),
    .rd_en(sram_rd), .memory_content(out_8), .data_out(controlled_buffer_1_out));
  sram_cell sram_cell_2 (
    .data_in(controlled_buffer_1_out), .wr_en(sram_wr), .clk(sram_clk), .cs(dec_4x16_1_dec_out[1]),
    .rd_en(sram_rd), .memory_content(out_9), .data_out(controlled_buffer_1_out));
  sram_cell sram_cell_3 (
    .data_in(controlled_buffer_1_out), .wr_en(sram_wr), .clk(sram_clk), .cs(dec_4x16_1_dec_out[2]),
    .rd_en(sram_rd), .memory_content(out_10), .data_out(controlled_buffer_1_out));
  sram_cell sram_cell_4 (
    .data_in(controlled_buffer_1_out), .wr_en(sram_wr), .clk(sram_clk), .cs(dec_4x16_1_dec_out[3]),
    .rd_en(sram_rd), .memory_content(out_11), .data_out(controlled_buffer_1_out));
  sram_cell sram_cell_5 (
    .data_in(controlled_buffer_1_out), .wr_en(sram_wr), .clk(sram_clk), .cs(dec_4x16_1_dec_out[4]),
    .rd_en(sram_rd), .memory_content(out_12), .data_out(controlled_buffer_1_out));
  sram_cell sram_cell_6 (
    .data_in(controlled_buffer_1_out), .wr_en(sram_wr), .clk(sram_clk), .cs(dec_4x16_1_dec_out[5]),
    .rd_en(sram_rd), .memory_content(out_13), .data_out(controlled_buffer_1_out));
  sram_cell sram_cell_7 (
    .data_in(controlled_buffer_1_out), .wr_en(sram_wr), .clk(sram_clk), .cs(dec_4x16_1_dec_out[6]),
    .rd_en(sram_rd), .memory_content(out_14), .data_out(controlled_buffer_1_out));
  sram_cell sram_cell_8 (
    .data_in(controlled_buffer_1_out), .wr_en(sram_wr), .clk(sram_clk), .cs(dec_4x16_1_dec_out[7]),
    .rd_en(sram_rd), .memory_content(out_15), .data_out(controlled_buffer_1_out));
  sram_cell sram_cell_9 (
    .data_in(controlled_buffer_1_out), .wr_en(sram_wr), .clk(sram_clk), .cs(dec_4x16_1_dec_out[8]),
    .rd_en(sram_rd), .memory_content(out_16), .data_out(controlled_buffer_1_out));
  sram_cell sram_cell_10 (
    .data_in(controlled_buffer_1_out), .wr_en(sram_wr), .clk(sram_clk), .cs(dec_4x16_1_dec_out[9]),
    .rd_en(sram_rd), .memory_content(out_17), .data_out(controlled_buffer_1_out));
  sram_cell sram_cell_11 (
    .data_in(controlled_buffer_1_out), .wr_en(sram_wr), .clk(sram_clk), .cs(dec_4x16_1_dec_out[10]),
    .rd_en(sram_rd), .memory_content(out_18), .data_out(controlled_buffer_1_out));
  sram_cell sram_cell_12 (
    .data_in(controlled_buffer_1_out), .wr_en(sram_wr), .clk(sram_clk), .cs(dec_4x16_1_dec_out[11]),
    .rd_en(sram_rd), .memory_content(out_19), .data_out(controlled_buffer_1_out));
  sram_cell sram_cell_13 (
    .data_in(controlled_buffer_1_out), .wr_en(sram_wr), .clk(sram_clk), .cs(dec_4x16_1_dec_out[12]),
    .rd_en(sram_rd), .memory_content(out_20), .data_out(controlled_buffer_1_out));
  sram_cell sram_cell_14 (
    .data_in(controlled_buffer_1_out), .wr_en(sram_wr), .clk(sram_clk), .cs(dec_4x16_1_dec_out[13]),
    .rd_en(sram_rd), .memory_content(out_21), .data_out(controlled_buffer_1_out));
  sram_cell sram_cell_15 (
    .data_in(controlled_buffer_1_out), .wr_en(sram_wr), .clk(sram_clk), .cs(dec_4x16_1_dec_out[14]),
    .rd_en(sram_rd), .memory_content(out_22), .data_out(controlled_buffer_1_out));
  sram_cell sram_cell_16 (
    .data_in(controlled_buffer_1_out), .wr_en(sram_wr), .clk(sram_clk), .cs(dec_4x16_1_dec_out[15]),
    .rd_en(sram_rd), .memory_content(out_23), .data_out(controlled_buffer_1_out));
  assign sram_d_out = sram_rd ? controlled_buffer_1_out : 8'bz;  // Controlled_Buffer controlled_buffer_2
endmodule

module Ins_reg (
  input  [7:0] ins_reg_in,
  input  ins_reg_in_en,
  input  clk,
  input  ins_reg_out_en,
  output [3:0] add_outs,
  output [3:0] ins_out
);

  wire [3:0] reg_gp_1_reg_int_out;

  reg_gp reg_gp_1 (
    .reg_in(ins_reg_in), .reg_in_en(ins_reg_in_en), .reg_clk(clk),
    .reg_int_out({ins_out, reg_gp_1_reg_int_out}));  // open: reg_out_en, reg_out
  assign add_outs = ins_reg_out_en ? reg_gp_1_reg_int_out : 4'bz;  // Controlled_Buffer controlled_buffer_1
endmodule

module pc (
  input  pc_en,
  input  pc_clk,
  input  pc_reset,
  input  pc_out_en,
  output [3:0] pc_value,
  output [3:0] pc_out
);

  wire j_k_ff_2_qn, j_k_ff_3_qn, j_k_ff_4_qn;

  J_K_Flip_Flop j_k_ff_1 (
    .J(pc_en), .K(pc_en), .clk(j_k_ff_2_qn), .Q(pc_value[3]), .reset(pc_reset));  // open: Qn, preset
  J_K_Flip_Flop j_k_ff_2 (
    .J(pc_en), .K(pc_en), .clk(j_k_ff_3_qn), .Q(pc_value[2]), .Qn(j_k_ff_2_qn), .reset(pc_reset));  // open: preset
  J_K_Flip_Flop j_k_ff_3 (
    .J(pc_en), .K(pc_en), .clk(j_k_ff_4_qn), .Q(pc_value[1]), .Qn(j_k_ff_3_qn), .reset(pc_reset));  // open: preset
  J_K_Flip_Flop j_k_ff_4 (
    .J(pc_en), .K(pc_en), .clk(pc_clk), .Q(pc_value[0]), .Qn(j_k_ff_4_qn), .reset(pc_reset));  // open: preset
  assign pc_out = pc_out_en ? pc_value : 4'bz;  // Controlled_Buffer controlled_buffer_1

  // Notes on the sheet:
  //          Clock
  //         Reset
  //   Output Control
  //               Count Control
  //                   Counter Output
endmodule

module rc (
  input  clk,
  input  ring_reset,
  output T1,
  output T2,
  output T3,
  output T4,
  output T5,
  output T6
);

  wire controlled_buffer_1_out, not_1_out;
  wire [3:0] pc_1_pc_value;
  wire [15:6] dec_4x16_1_dec_out;

  assign controlled_buffer_1_out = ring_reset ? ring_reset : 1'bz;  // Controlled_Buffer controlled_buffer_1
  not not_1 (not_1_out, ring_reset);
  assign controlled_buffer_1_out = not_1_out ? dec_4x16_1_dec_out[6] : 1'bz;  // Controlled_Buffer controlled_buffer_2
  pc pc_1 (
    .pc_en(1'b1), .pc_clk(clk), .pc_reset(controlled_buffer_1_out), .pc_out_en(1'b1), .pc_value(pc_1_pc_value));  // open: pc_out
  dec_4x16 dec_4x16_1 (.dec_sel(pc_1_pc_value), .dec_out({dec_4x16_1_dec_out, T6, T5, T4, T3, T2, T1}));
endmodule

module ins_dec (
  input  [3:0] ir_msb,
  output isLDA,
  output isLDB,
  output isADD,
  output isSUB,
  output isSTA,
  output isJMP,
  output isHLT
);

  wire [14:0] dec_4x16_1_dec_out;

  dec_4x16 dec_4x16_1 (
    .dec_sel(ir_msb),
    .dec_out({isHLT, dec_4x16_1_dec_out[14:7], isJMP, isSTA, isSUB, isADD, isLDB, isLDA, dec_4x16_1_dec_out[0]}));
endmodule

module control_sequence (
  input  clk,
  input  clk_reset,
  input  [3:0] ins_msb,
  input  L1,
  input  debug,
  input  l2,
  output mar_in_en_final,
  output pc_en,
  output pc_out_final,
  output sram_rd_final,
  output jmp_en,
  output ins_reg_in_en,
  output hlt,
  output a_in,
  output a_out_final,
  output b_in,
  output sub_out,
  output ins_reg_out_en,
  output sram_wr_final,
  output alu_out
);

  wire and_1_out, and_4_out, and_5_out, and_6_out, and_7_out, and_9_out, and_10_out, and_11_out, and_13_out,
       and_15_out, and_16_out, and_17_out, and_18_out, and_19_out, and_21_out, and_23_out, and_24_out,
       and_27_out, and_28_out, and_29_out, and_30_out, and_31_out, ins_dec_1_isadd, ins_dec_1_ishlt,
       ins_dec_1_isjmp, ins_dec_1_islda, ins_dec_1_isldb, ins_dec_1_issta, ins_dec_1_issub, not_1_out,
       not_2_out, not_3_out, or_1_out, or_3_out, or_4_out, or_5_out, or_6_out, rc_1_t1, rc_1_t2, rc_1_t4,
       rc_1_t5;

  not not_1 (not_1_out, debug);
  not not_2 (not_2_out, debug);
  not not_3 (not_3_out, l2);
  rc rc_1 (
    .clk(clk), .ring_reset(clk_reset), .T1(rc_1_t1), .T2(rc_1_t2), .T3(pc_en), .T4(rc_1_t4), .T5(rc_1_t5));  // open: T6
  ins_dec ins_dec_1 (
    .ir_msb(ins_msb), .isLDA(ins_dec_1_islda), .isLDB(ins_dec_1_isldb), .isADD(ins_dec_1_isadd),
    .isSUB(ins_dec_1_issub), .isSTA(ins_dec_1_issta), .isJMP(ins_dec_1_isjmp), .isHLT(ins_dec_1_ishlt));
  and and_1 (and_1_out, pc_en, ins_dec_1_isjmp);
  and and_2 (jmp_en, not_3_out, and_1_out, not_2_out);
  and and_3 (pc_out_final, not_2_out, not_3_out, rc_1_t1);
  and and_4 (and_4_out, ins_dec_1_islda, rc_1_t4);
  or or_1 (or_1_out, rc_1_t1, and_4_out, and_6_out, and_7_out);
  and and_5 (and_5_out, not_1_out, or_1_out);
  or or_2 (mar_in_en_final, and_5_out, L1);
  and and_6 (and_6_out, ins_dec_1_isldb, rc_1_t4);
  and and_7 (and_7_out, ins_dec_1_issta, rc_1_t4);
  or or_3 (or_3_out, rc_1_t2, and_9_out, and_10_out);
  and and_8 (sram_rd_final, not_2_out, not_3_out, or_3_out);
  and and_9 (and_9_out, rc_1_t5, ins_dec_1_islda);
  and and_10 (and_10_out, rc_1_t5, ins_dec_1_isldb);
  and and_11 (and_11_out, ins_dec_1_isjmp, pc_en);
  and and_12 (ins_reg_in_en, not_2_out, not_3_out, rc_1_t2);
  and and_13 (and_13_out, rc_1_t4, ins_dec_1_islda);
  and and_14 (ins_reg_out_en, not_2_out, not_3_out, or_4_out);
  and and_15 (and_15_out, rc_1_t4, ins_dec_1_isldb);
  and and_16 (and_16_out, rc_1_t4, ins_dec_1_issta);
  or or_4 (or_4_out, and_11_out, and_13_out, and_15_out, and_16_out);
  and and_17 (and_17_out, rc_1_t4, ins_dec_1_issub);
  and and_18 (and_18_out, rc_1_t4, ins_dec_1_isadd);
  and and_19 (and_19_out, rc_1_t5, ins_dec_1_islda);
  or or_5 (or_5_out, and_17_out, and_19_out, and_18_out);
  and and_20 (a_in, not_2_out, not_3_out, or_5_out);
  and and_21 (and_21_out, rc_1_t5, ins_dec_1_issta);
  and and_22 (a_out_final, not_2_out, not_3_out, and_21_out);
  and and_23 (and_23_out, rc_1_t5, ins_dec_1_isldb);
  and and_24 (and_24_out, rc_1_t4, ins_dec_1_isadd);
  and and_25 (b_in, not_2_out, not_3_out, and_23_out);
  and and_26 (alu_out, not_2_out, not_3_out, or_6_out);
  and and_27 (and_27_out, ins_dec_1_issub, rc_1_t4);
  or or_6 (or_6_out, and_24_out, and_27_out);
  and and_28 (and_28_out, not_3_out, and_29_out);
  or or_7 (sram_wr_final, l2, and_28_out);
  and and_29 (and_29_out, rc_1_t5, ins_dec_1_issta);
  and and_30 (and_30_out, ins_dec_1_ishlt, rc_1_t4);
  and and_31 (and_31_out, ins_dec_1_issub, rc_1_t4);
  and and_32 (hlt, not_2_out, not_3_out, and_30_out);
  and and_33 (sub_out, not_3_out, not_2_out, and_31_out);
endmodule

module ins_loader (
  input  bc_reset,
  input  bc_enable,
  input  clk,
  input  debug,
  output [3:0] bc_address,
  output L1,
  output L2
);

  wire controlled_buffer_1_out, d_ff_1_q, not_1_out;

  Counter #(.max('hf), .width(4)) counter_1 (
    .clr(bc_reset), .load(1'b0), .up(1'b1), .count(bc_enable), .clk(clk), .Q(bc_address));  // open: D, carry
  assign controlled_buffer_1_out = debug ? not_1_out : 1'bz;  // Controlled_Buffer controlled_buffer_1
  D_Flip_Flop d_ff_1 (.D(controlled_buffer_1_out), .clk(clk), .Q(d_ff_1_q));  // open: Qn, preset, reset
  not not_1 (not_1_out, d_ff_1_q);
  and and_1 (L1, debug, not_1_out);
  and and_2 (L2, debug, d_ff_1_q);
endmodule

module pc_with_loader (
  input  pc_reset,
  input  load_or_count,
  input  pc_en,
  input  clk,
  input  [3:0] data_load,
  input  pc_out_en,
  output [3:0] pc_value,
  output [3:0] pc_out
);

  Counter #(.max('hf), .width(4)) counter_1 (
    .clr(pc_reset), .load(load_or_count), .up(1'b1), .count(pc_en), .clk(clk), .D(data_load), .Q(pc_value));  // open: carry
  assign pc_out = pc_out_en ? pc_value : 4'bz;  // Controlled_Buffer controlled_buffer_1
endmodule
